// Logisim project Composants.circ as structural Verilog: 2 circuits, main circuit banc_reg
module banc_reg (
  input  clk,
  input  [31:0] ValEcriture,
  input  [3:0] IndReg0,
  input  [3:0] IndReg1,
  input  [3:0] IndRegEcr,
  input  SigEcr,
  input  [31:0] R15_in,
  output [31:0] ValReg0,
  output [31:0] Valreg1
);

  wire demultiplexer_1_out0, demultiplexer_1_out1, demultiplexer_1_out2, demultiplexer_1_out3,
       demultiplexer_1_out4, demultiplexer_1_out5, demultiplexer_1_out6, demultiplexer_1_out7,
       demultiplexer_1_out8, demultiplexer_1_out9, demultiplexer_1_out10, demultiplexer_1_out11,
       demultiplexer_1_out12, demultiplexer_1_out13, demultiplexer_1_out14;
  wire [31:0] r0_q, r1_q, r2_q, r3_q, r4_q, r5_q, r6_q, r7_q, r8_q, r9_q, r10_q, r11_q, r12_q, r13_q, r14_q,
       r15_q;

  Demultiplexer #(.select(4)) demultiplexer_1 (
    .out0(demultiplexer_1_out0), .out1(demultiplexer_1_out1), .out2(demultiplexer_1_out2),
    .out3(demultiplexer_1_out3), .out4(demultiplexer_1_out4), .out5(demultiplexer_1_out5),
    .out6(demultiplexer_1_out6), .out7(demultiplexer_1_out7), .out8(demultiplexer_1_out8),
    .out9(demultiplexer_1_out9), .out10(demultiplexer_1_out10), .out11(demultiplexer_1_out11),
    .out12(demultiplexer_1_out12), .out13(demultiplexer_1_out13), .out14(demultiplexer_1_out14), .in(SigEcr),
    .sel(IndRegEcr));  // open: out15
  Register #(.width(32)) r0 (.D(ValEcriture), .en(demultiplexer_1_out0), .clk(clk), .Q(r0_q));  // open: clr
  Register #(.width(32)) r1 (.D(ValEcriture), .en(demultiplexer_1_out1), .clk(clk), .Q(r1_q));  // open: clr
  Register #(.width(32)) r2 (.D(ValEcriture), .en(demultiplexer_1_out2), .clk(clk), .Q(r2_q));  // open: clr
  Register #(.width(32)) r3 (.D(ValEcriture), .en(demultiplexer_1_out3), .clk(clk), .Q(r3_q));  // open: clr
  Register #(.width(32)) r4 (.D(ValEcriture), .en(demultiplexer_1_out4), .clk(clk), .Q(r4_q));  // open: clr
  Register #(.width(32)) r5 (.D(ValEcriture), .en(demultiplexer_1_out5), .clk(clk), .Q(r5_q));  // open: clr
  Register #(.width(32)) r6 (.D(ValEcriture), .en(demultiplexer_1_out6), .clk(clk), .Q(r6_q));  // open: clr
  Register #(.width(32)) r7 (.D(ValEcriture), .en(demultiplexer_1_out7), .clk(clk), .Q(r7_q));  // open: clr
  Register #(.width(32)) r8 (.D(ValEcriture), .en(demultiplexer_1_out8), .clk(clk), .Q(r8_q));  // open: clr
  Register #(.width(32)) r9 (.D(ValEcriture), .en(demultiplexer_1_out9), .clk(clk), .Q(r9_q));  // open: clr
  Register #(.width(32)) r10 (.D(ValEcriture), .en(demultiplexer_1_out10), .clk(clk), .Q(r10_q));  // open: clr
  Register #(.width(32)) r11 (.D(ValEcriture), .en(demultiplexer_1_out11), .clk(clk), .Q(r11_q));  // open: clr
  Register #(.width(32)) r12 (.D(ValEcriture), .en(demultiplexer_1_out12), .clk(clk), .Q(r12_q));  // open: clr
  Register #(.width(32)) r13 (.D(ValEcriture), .en(demultiplexer_1_out13), .clk(clk), .Q(r13_q));  // open: clr
  Register #(.width(32)) r14 (.D(ValEcriture), .en(demultiplexer_1_out14), .clk(clk), .Q(r14_q));  // open: clr
  Register #(.width(32)) r15 (.D(R15_in), .en(1'b1), .clk(clk), .Q(r15_q));  // open: clr
  Multiplexer #(.select(4), .width(32)) multiplexer_1 (
    .in0(r0_q), .in1(r1_q), .in2(r2_q), .in3(r3_q), .in4(r4_q), .in5(r5_q), .in6(r6_q), .in7(r7_q),
    .in8(r8_q), .in9(r9_q), .in10(r10_q), .in11(r11_q), .in12(r12_q), .in13(r13_q), .in14(r14_q),
    .in15(r15_q), .out(ValReg0), .sel(IndReg0));
  Multiplexer #(.select(4), .width(32)) multiplexer_2 (
    .in0(r0_q), .in1(r1_q), .in2(r2_q), .in3(r3_q), .in4(r4_q), .in5(r5_q), .in6(r6_q), .in7(r7_q),
    .in8(r8_q), .in9(r9_q), .in10(r10_q), .in11(r11_q), .in12(r12_q), .in13(r13_q), .in14(r14_q),
    .in15(r15_q), .out(Valreg1), .sel(IndReg1));
endmodule

module ALU (
  input  [31:0] Op1,
  input  [31:0] Op2,
  input  [1:0] Sel,
  output [31:0] Sortie,
  output [3:0] NZCV
);

  wire adder_1_cout, and_1_out, multiplexer_1_out, not_1_out, not_2_out, or_1_out, subtractor_1_bout,
       xor_1_out, xor_2_out;
  wire [31:0] adder_1_out, and_3_out, subtractor_1_out;

  ExactlyOne xor_1 (.out(xor_1_out), .in0(Sel[0]), .in1(Op2[31]), .in2(Op1[31]));
  not not_1 (not_1_out, xor_1_out);
  and and_1 (and_1_out, not_1_out, xor_2_out);
  and and_2 (NZCV[0], Sel[1], and_1_out);
  xor xor_2 (xor_2_out, Op1[31], NZCV[3]);
  assign and_3_out = Op1 & Op2;  // AND_Gate and_3, 32 bits wide
  Adder #(.width(32)) adder_1 (.a(Op1), .b(Op2), .out(adder_1_out), .cout(adder_1_cout));  // open: cin
  Subtractor #(.width(32)) subtractor_1 (
    .a(Op1), .b(Op2), .out(subtractor_1_out), .bout(subtractor_1_bout));  // open: bin
  not not_2 (not_2_out, subtractor_1_bout);
  Multiplexer multiplexer_1 (.in0(adder_1_cout), .in1(not_2_out), .out(multiplexer_1_out), .sel(Sel[0]));
  Multiplexer multiplexer_2 (.in0(1'b0), .in1(multiplexer_1_out), .out(NZCV[1]), .sel(Sel[1]));
  Multiplexer #(.select(2), .width(32)) multiplexer_3 (
    .in0(and_3_out), .in1(Op2), .in2(adder_1_out), .in3(subtractor_1_out), .out({NZCV[3], Sortie[30:0]}),
    .sel(Sel));
  or or_1 (or_1_out, NZCV[3], Sortie[30], Sortie[29], Sortie[28], Sortie[27], Sortie[26], Sortie[25], Sortie[24], Sortie[23], Sortie[22], Sortie[21], Sortie[20], Sortie[19], Sortie[18], Sortie[17], Sortie[16], Sortie[15], Sortie[14], Sortie[13], Sortie[11], Sortie[10], Sortie[9], Sortie[8], Sortie[7], Sortie[6], Sortie[5], Sortie[4], Sortie[3], Sortie[2], Sortie[1], Sortie[0], Sortie[12]);
  not not_3 (NZCV[2], or_1_out);

  assign Sortie[31] = NZCV[3];
endmodule
