// Logisim project TP1.circ as structural Verilog: 7 circuits, main circuit main
module main (
  input  CLK
);

  wire and_1_out, and_2_out, decodeur_1_branch, decodeur_1_imm_reg, decodeur_1_s, gestion_conditions_1_exec,
       not_1_out;
  wire [1:0] decodeur_1_op;
  wire [3:0] alu_1_nzcv, decodeur_1_cond, decodeur_1_rd, decodeur_1_rot, decodeur_1_rs1, decodeur_1_rs2;
  wire [7:0] decodeur_1_imm, undriven;
  wire [15:0] undriven_2;
  wire [23:0] decodeur_1_offset, r15_pc_q_2;
  wire [31:0] add4_1_sortie, adder_1_out, alu_1_sortie, banc_reg_1_valreg0, banc_reg_1_valreg1,
       calculateur_imm_1_imm_final, multiplexer_1_out, multiplexer_2_out, r15_pc_q, ram_1_dout;
  wire [31:31] undriven_3;

  RAM #(.addrWidth(24), .asyncread("true"), .dataWidth(32)) ram_1 (
    .addr(r15_pc_q_2), .oe(1'b1), .dout(ram_1_dout));  // open: we, clk, din
  add4 add4_1 (.entree({r15_pc_q[31:26], r15_pc_q_2, r15_pc_q[1:0]}), .sortie(add4_1_sortie));
  decodeur decodeur_1 (
    .Instr(ram_1_dout), .Rs1(decodeur_1_rs1), .Rs2(decodeur_1_rs2), .Rd(decodeur_1_rd), .Imm(decodeur_1_imm),
    .Rot(decodeur_1_rot), .Imm_reg(decodeur_1_imm_reg), .Op(decodeur_1_op), .S(decodeur_1_s),
    .Cond(decodeur_1_cond), .Offset(decodeur_1_offset), .Branch(decodeur_1_branch));  // open: L
  Multiplexer #(.width(32)) multiplexer_1 (
    .in0(adder_1_out), .in1(add4_1_sortie), .out(multiplexer_1_out), .sel(decodeur_1_branch));
  Register #(.width(32)) r15_pc (
    .D(multiplexer_1_out), .en(1'b1), .clk(CLK), .Q({r15_pc_q[31:26], r15_pc_q_2, r15_pc_q[1:0]}));  // open: clr
  Adder #(.width(32)) adder_1 (
    .a({r15_pc_q[31:26], r15_pc_q_2, r15_pc_q[1:0]}), .b({undriven_3[31], {7{1'b0}}, undriven_2, undriven}),
    .out(adder_1_out));  // open: cin, cout
  // Probe on banc_reg_1_valreg0
  banc_reg banc_reg_1 (
    .clk(CLK), .ValEcriture(alu_1_sortie), .IndReg0(decodeur_1_rs1), .IndReg1(decodeur_1_rs2),
    .IndRegEcr(decodeur_1_rd), .SigEcr(and_2_out), .R15_in({r15_pc_q[31:26], r15_pc_q_2, r15_pc_q[1:0]}),
    .ValReg0(banc_reg_1_valreg0), .Valreg1(banc_reg_1_valreg1));
  // Probe on banc_reg_1_valreg1
  calculateur_imm calculateur_imm_1 (
    .imm(decodeur_1_imm), .rotate(decodeur_1_rot), .imm_final(calculateur_imm_1_imm_final));
  Multiplexer #(.width(32)) multiplexer_2 (
    .in0(banc_reg_1_valreg1), .in1(calculateur_imm_1_imm_final), .out(multiplexer_2_out),
    .sel(decodeur_1_imm_reg));
  not not_1 (not_1_out, decodeur_1_branch);
  and and_1 (and_1_out, decodeur_1_s, not_1_out);
  ALU alu_1 (
    .Op1(banc_reg_1_valreg0), .Op2(multiplexer_2_out), .Sel(decodeur_1_op), .Sortie(alu_1_sortie),
    .NZCV(alu_1_nzcv));
  gestion_conditions gestion_conditions_1 (
    .cond(decodeur_1_cond), .NZCV(alu_1_nzcv), .Maj(and_1_out), .clk(CLK), .Exec(gestion_conditions_1_exec));
  and and_2 (and_2_out, gestion_conditions_1_exec, not_1_out);
endmodule

module decodeur (
  input  [31:0] Instr,
  output [3:0] Rs1,
  output [3:0] Rs2,
  output [3:0] Rd,
  output [7:0] Imm,
  output [3:0] Rot,
  output Imm_reg,
  output [1:0] Op,
  output S,
  output [3:0] Cond,
  output [23:0] Offset,
  output L,
  output Branch
);

  wire egal_4bit_1_res, not_1_out;

  not not_1 (not_1_out, Instr[25]);
  egal_4bit egal_4bit_1 (.A(4'b1010), .B(Instr[24:21]), .res(egal_4bit_1_res));
  decodeur_opcode decodeur_opcode_1 (.OpCode(Instr[24:21]), .Op(Op));
  and and_1 (Branch, not_1_out, Instr[26]);
  Multiplexer #(.width(4)) multiplexer_1 (.in0(Instr[15:12]), .in1(4'b1111), .out(Rd), .sel(egal_4bit_1_res));

  assign Cond = Instr[31:28];
  assign Imm = Instr[7:0];
  assign Imm_reg = Instr[25];
  assign L = Instr[24];
  assign Offset = Instr[23:0];
  assign Rot = Instr[11:8];
  assign Rs1 = Instr[19:16];
  assign Rs2 = Instr[3:0];
  assign S = Instr[20];
endmodule

module decodeur_opcode (
  input  [3:0] OpCode,
  output [1:0] Op
);

  wire and_1_out, not_1_out;

  not not_1 (not_1_out, OpCode[3]);
  and and_1 (and_1_out, OpCode[2], not_1_out);
  or or_1 (Op[0], OpCode[0], OpCode[1]);
  or or_2 (Op[1], OpCode[1], and_1_out);
endmodule

module calculateur_imm (
  input  [7:0] imm,
  input  [3:0] rotate,
  output [31:0] imm_final
);

  Shifter #(.shift("rr"), .width(32)) shifter_1 (.in({{24{1'b0}}, imm}), .\dist ({rotate, 1'b0}), .out(imm_final));
endmodule

module add4 (
  input  [31:0] entree,
  output [31:0] sortie
);

  Adder #(.width(32)) adder_1 (.a(entree), .b(32'h4), .out(sortie));  // open: cin, cout
endmodule

module gestion_conditions (
  input  [3:0] cond,
  input  [3:0] NZCV,
  input  Maj,
  input  clk,
  output Exec
);

  wire and_1_out, and_2_out, and_3_out, and_4_out, and_5_out, and_6_out, and_7_out, and_8_out, and_9_out,
       and_10_out, and_11_out, and_12_out, and_13_out, and_14_out, and_15_out, and_16_out, not_1_out,
       not_2_out, not_3_out, not_4_out, not_5_out, not_6_out, not_7_out, or_1_out, or_2_out, xnor_1_out,
       xnor_2_out, xor_1_out, xor_2_out;
  wire [3:0] register_1_q;
  wire [15:0] decoder_1_out0;

  Register #(.width(4)) register_1 (.D(NZCV), .en(Maj), .clk(clk), .Q(register_1_q));  // open: clr
  Decoder #(.select(4)) decoder_1 (
    .out0(decoder_1_out0[0]), .out1(decoder_1_out0[1]), .out2(decoder_1_out0[2]), .out3(decoder_1_out0[3]),
    .out4(decoder_1_out0[4]), .out5(decoder_1_out0[5]), .out6(decoder_1_out0[6]), .out7(decoder_1_out0[7]),
    .out8(decoder_1_out0[8]), .out9(decoder_1_out0[9]), .out10(decoder_1_out0[10]),
    .out11(decoder_1_out0[11]), .out12(decoder_1_out0[12]), .out13(decoder_1_out0[13]),
    .out14(decoder_1_out0[14]), .out15(decoder_1_out0[15]), .sel(cond), .en(1'b1));
  not not_1 (not_1_out, register_1_q[2]);
  not not_2 (not_2_out, register_1_q[1]);
  not not_3 (not_3_out, register_1_q[3]);
  not not_4 (not_4_out, register_1_q[0]);
  not not_5 (not_5_out, register_1_q[2]);
  and and_1 (and_1_out, not_5_out, register_1_q[1]);
  or or_1 (or_1_out, register_1_q[2], not_6_out);
  not not_6 (not_6_out, register_1_q[1]);
  xnor xnor_1 (xnor_1_out, register_1_q[3], register_1_q[0]);
  xor xor_1 (xor_1_out, register_1_q[3], register_1_q[0]);
  xnor xnor_2 (xnor_2_out, register_1_q[3], register_1_q[0]);
  and and_2 (and_2_out, xnor_2_out, not_7_out);
  not not_7 (not_7_out, register_1_q[2]);
  xor xor_2 (xor_2_out, register_1_q[3], register_1_q[0]);
  or or_2 (or_2_out, xor_2_out, register_1_q[2]);
  and and_3 (and_3_out, decoder_1_out0[0], register_1_q[2]);
  and and_4 (and_4_out, decoder_1_out0[1], not_1_out);
  and and_5 (and_5_out, decoder_1_out0[2], register_1_q[1]);
  and and_6 (and_6_out, decoder_1_out0[3], not_2_out);
  and and_7 (and_7_out, decoder_1_out0[4], register_1_q[3]);
  and and_8 (and_8_out, decoder_1_out0[5], not_3_out);
  and and_9 (and_9_out, decoder_1_out0[6], register_1_q[0]);
  and and_10 (and_10_out, decoder_1_out0[7], not_4_out);
  and and_11 (and_11_out, decoder_1_out0[8], and_1_out);
  and and_12 (and_12_out, decoder_1_out0[9], or_1_out);
  and and_13 (and_13_out, decoder_1_out0[10], xnor_1_out);
  and and_14 (and_14_out, decoder_1_out0[11], xor_1_out);
  and and_15 (and_15_out, decoder_1_out0[12], and_2_out);
  and and_16 (and_16_out, decoder_1_out0[13], or_2_out);
  or or_3 (Exec, and_3_out, and_4_out, and_5_out, and_6_out, and_7_out, and_8_out, and_9_out, and_10_out, and_11_out, and_12_out, and_13_out, and_14_out, and_15_out, and_16_out, decoder_1_out0[14]);
endmodule

module egal_4bit (
  input  [3:0] A,
  input  [3:0] B,
  output res
);

  wire xnor_1_out, xnor_2_out, xnor_3_out, xnor_4_out;

  xnor xnor_1 (xnor_1_out, A[0], B[0]);
  xnor xnor_2 (xnor_2_out, A[1], B[1]);
  xnor xnor_3 (xnor_3_out, A[2], B[2]);
  xnor xnor_4 (xnor_4_out, A[3], B[3]);
  and and_1 (res, xnor_1_out, xnor_2_out, xnor_3_out, xnor_4_out);
endmodule
